// Logisim project Crc_4bits_teste.circ as structural Verilog: 3 circuits, main circuit crc
module crc (
  input  in_1,
  input  in_2,
  input  [4:0] Polinomio,
  input  in_4,
  output erro,
  output [3:0] out_6
);

  wire c0_sxor, clk, ram_1_p1, ram_1_p5, sc0, sc1, sc2, sc3, sc4;

  // RAM #(.addrWidth(4), .dataWidth(1), .databus("bibus")) ram_1: pin names not known; wires that end beside it: ram_1_p1, out_6, ram_1_p1, clk, ram_1_p5
  cont15 cont15_1 (
    .rst(in_2), .start_cont(in_1), .clk(clk), .c0(out_6[0]), .c1(out_6[1]), .c2(out_6[2]), .c3(out_6[3]));
  pt1_crc c0 (.Entrada(sc4), .Poli(Polinomio[0]), .Dado(in_4), .Clock(clk), .Reset(in_2), .sXOR(c0_sxor), .Saida(sc0));
  pt1_crc c1 (
    .Entrada(c0_sxor), .Poli(Polinomio[1]), .Dado(sc0), .Clock(clk), .Reset(in_2), .Saida(sc1));  // open: sXOR
  pt1_crc c2 (
    .Entrada(c0_sxor), .Poli(Polinomio[2]), .Dado(sc1), .Clock(clk), .Reset(in_2), .Saida(sc2));  // open: sXOR
  pt1_crc c3 (
    .Entrada(c0_sxor), .Poli(Polinomio[3]), .Dado(sc2), .Clock(clk), .Reset(in_2), .Saida(sc3));  // open: sXOR
  or or_1 (erro, sc0, sc1, sc2, sc3, sc4);
  pt1_crc pt1_crc_1 (
    .Entrada(c0_sxor), .Poli(Polinomio[4]), .Dado(sc3), .Clock(clk), .Reset(in_2), .Saida(sc4));  // open: sXOR

  // Other names for the same wires on the sheet: Cont[3:0] = out_6; reset = in_2; start = in_1
endmodule

module pt1_crc (
  input  Entrada,
  input  Poli,
  input  Dado,
  input  Clock,
  input  Reset,
  output sXOR,
  output Saida
);

  wire and_1_out;

  and and_1 (and_1_out, Entrada, Poli);
  xor xor_1 (sXOR, and_1_out, Dado);
  D_Flip_Flop d_ff_1 (.D(sXOR), .clk(Clock), .Q(Saida), .reset(Reset));  // open: Qn, preset
endmodule

module cont15 (
  input  rst,
  input  start_cont,
  output clk,
  output c0,
  output c1,
  output c2,
  output c3
);

  wire and_1_out, clock_1_out, nand_1_out;
  wire [1:1] counter_1_q;

  Clock clock_1 (.out(clock_1_out));
  assign clk = and_1_out ? clock_1_out : 1'bz;  // Controlled_Buffer controlled_buffer_1
  and and_1 (and_1_out, start_cont, nand_1_out);
  Counter #(.width(4), .max('hf)) counter_1 (
    .clr(rst), .clk(clk), .Q({c3, c2, counter_1_q[1], c0}));  // open: load, up, count, D, carry
  nand nand_1 (nand_1_out, c0, counter_1_q[1], c2, c3);

  assign c1 = c0;
endmodule
